// Logisim project RV32I.circ as structural Verilog: 1 circuit, main circuit main
module main (
);

  wire clk;
  wire [2:0] instructiondecoder_1_funct3, instructiondecoder_1_type;
  wire [4:0] instructiondecoder_1_rd, instructiondecoder_1_rs1, instructiondecoder_1_rs2;
  wire [6:0] instructiondecoder_1_funct7;
  wire [31:0] adder_1_out, instructiondecoder_1_bimm, instructiondecoder_1_iimm, instructiondecoder_1_jimm,
       instructiondecoder_1_simm, instructiondecoder_1_uimm, main_1_data_out, main_2_rs1, main_2_rs2,
       multiplexer_1_out, PC_q;

  Clock Clock (.out(clk));
  Adder #(.width(32)) adder_1 (.a(PC_q), .b(32'h1), .out(adder_1_out));  // open: cin, cout
  Multiplexer #(.enable("false"), .width(32)) multiplexer_1 (
    .in0(adder_1_out), .out(multiplexer_1_out));  // open: in1, sel
  Register #(.width(32)) PC (.D(multiplexer_1_out), .Q(PC_q), .clk(clk));  // open: en, clr
  InstructionMemory_main main_1 (.data_out(main_1_data_out));  // open: address
  // Probe on instructiondecoder_1_type
  InstructionDecoder instructiondecoder_1 (
    .rd(instructiondecoder_1_rd), .funct3(instructiondecoder_1_funct3), .rs1(instructiondecoder_1_rs1),
    .rs2(instructiondecoder_1_rs2), .funct7(instructiondecoder_1_funct7), .\type (instructiondecoder_1_type),
    .IImm(instructiondecoder_1_iimm), .SImm(instructiondecoder_1_simm), .BImm(instructiondecoder_1_bimm),
    .UImm(instructiondecoder_1_uimm), .JImm(instructiondecoder_1_jimm), .Instruction(main_1_data_out));
  // Probe on instructiondecoder_1_rd
  // Probe on instructiondecoder_1_funct3
  // Probe on instructiondecoder_1_rs1
  // Probe on instructiondecoder_1_rs2
  // Probe on instructiondecoder_1_funct7
  RegFile_main main_2 (
    .rs1(main_2_rs1), .rs2(main_2_rs2), .sel_rs1(instructiondecoder_1_rs1),
    .sel_rs2(instructiondecoder_1_rs2), .write(clk), .rd(instructiondecoder_1_rd));  // open: rst, data, clk
  // ALU_main main_3: pin names not known
  // DataMemory_main main_4: pin names not known

  // Notes on the sheet:
  //   Add 1 because IMem 
  //   is accessible only in 
  //   multiples of 4 bytes 
  //   (since all instructions 
  //   are 32bits exactly)
endmodule
